# Fritzing sketch Light (saved by Fritzing 0.9.9b)
perfboards: 4

parts:
  JP1 = Header 1 [package=1x01_offset]
  JP2 = Header 1 [package=1x01_offset]  # not connected
  Q1 = NPN-Transistor [package="TO92 [THT]"]
  JP3 = Header 1 [package=1x01_offset]  # not connected
  JP4 = Header 1 [package=1x01_offset]
  R1 = Resistor [tolerance=±5% resistance=1M package="1206 [SMD]"]
  R2 = Resistor [tolerance=±5% resistance=1M package="1206 [SMD]"]
  JP5 = Header 1 [package=1x01_offset]
  JP6 = Header 1 [package=1x01_offset]
  Q2 = NPN-Transistor [package="TO92 [THT]"]
  M1 = RioRand LM2596
  M2 = RioRand LM2596
  M3 = RioRand LM2596
  JP7 = Header 1 [package=1x01_offset]
  JP8 = Header 1 [package=1x01_offset]
  U1 = LIPO-2000mAh [package=lipo-2000]
  A1 = cks pd65W  # not connected
  Q4 = npn-Powertransistor [package="TO220 [THT]"]  # not connected
  Q5 = npn-Powertransistor [package="TO220 [THT]"]  # not connected
  Q6 = npn-Powertransistor [package="TO220 [THT]"]  # not connected
  Q7 = npn-Powertransistor [package="TO220 [THT]"]  # not connected
  WeMos_D1_Mini_Relay_Shield_V1 = WeMos D1 Mini Relay Shield V2  # not connected
  WeMos_D1_Mini_Relay_Shield_V2 = WeMos D1 Mini Relay Shield V2  # not connected
  WeMos_D1_Mini_Relay_Shield_V3 = WeMos D1 Mini Relay Shield V2  # not connected

nets:
  N1: JP1.1, JP5.1
  N2: Q1.E, R1.Pin_1
  N3: Q1.C, JP6.1
  N4: JP4.1, Q2.B
  N5: R2.Pin_1, Q2.E
  N6: M1.Pin_1, JP7.1, U1.+
  N7: M1.Pin_4, M2.Pin_4, M3.Pin_4
  N8: M2.Pin_1, M3.Pin_1
  N9: JP8.1, U1.-

notes:
  Headlight
  Horn1
  Horn2
  bot right: 12V in
  left rail GND
  Right rail PWR
  Right PWR Left GND
  12V in from Battery
  That is an xt60
  buck converters are 8 width not 9
  12V
  GND
  7V (green)
  GND
  5V (yellow)
  GND
  3.3V(orange)
  GND
  Use BIG WIRE

custom parts:
  cks pd65W: QC4.0 QC3.0 Type-C USB PD65W Fast Charging Adapter Module DC8-32V 3.25A 65W Step Down Module For Huawei SCP/FCP Apple PD.
